# Fritzing sketch Raspi_TTL (saved by Fritzing 0.9.10b)

parts:
  USBTTL1 = USB TTL Serial Cable
  Mod1 = Raspberry Pi 4B

nets:
  N1: USBTTL1.RX, Mod1.GPIO14
  N2: USBTTL1.TX, Mod1.GPIO15
  GND: USBTTL1.GND, Mod1.GND
