# Fritzing sketch TrinketM0_NRF24L01 (saved by Fritzing 0.9.10b)

parts:
  Part1 = NRF24L01+ Breakout Board
  Part2 = Adafruit Trinket M0 [part_number="Adafruit #3500"]

nets:
  GND: Part1.GND, Part2.GND
  VCC: Part1.VCC, Part2.3.3V
  N1: Part1.CE, Part2.D1_A0_PA02
  N2: Part1.CS, Part2.D0_A4_PA08_SDA
  N3: Part1.SCK, Part2.D3_A3_PA07_RXD_SCK
  N4: Part1.MOSI, Part2.D4_A2_PA06_TXD_MOSI
  N5: Part1.MISO, Part2.D2_A1_PA09_SCL_MISO
