# Fritzing sketch LCD_Trinket_NRF24L01 (saved by Fritzing 0.9.10b)
breadboards: 1

parts:
  Mod1 = Amica NodeMCU DEVKIT 1.0
  Grove1 = Grove OLED 128x96
  Part1 = NRF24L01+ Breakout Board

nets:
  N1: Mod1.pin1, Mod1.pin_26, Part1.VCC
  GND: Mod1.pin2, Mod1.pin_25, Mod1.pin_29, Grove1.GND, Part1.GND
  N2: Mod1.pin6, Part1.MOSI
  N3: Mod1.pin7, Part1.MISO
  N4: Mod1.pin8, Part1.SCK
  N5: Mod1.pin_11, Part1.CS
  N6: Mod1.pin_12, Part1.CE
  N7: Mod1.pin_13, Grove1.SDA
  N8: Mod1.pin_14, Grove1.SCL
  N9: Mod1.pin_30, Grove1.VCC
